// Logisim project new_arc.circ as structural Verilog: 9 circuits, main circuit main
module main (
  output [12:0] out_1,
  output [7:0] out_2,
  output [7:0] out_3,
  output [7:0] out_4,
  output [7:0] out_5,
  output [7:0] out_6
);

  wire clock_1_out, not_1_out;
  wire [1:0] alu_and_regesters_1_out_8;
  wire [6:0] instruction_reg_1_out_5, instruction_reg_1_out_6;
  wire [7:0] alu_and_regesters_1_out_6, multiplexer_1_out;
  wire [8:0] instruction_reg_1_out_7;

  Clock clock_1 (.out(clock_1_out));
  instruction_reg instruction_reg_1 (
    .clk(out_5), .in_2(clock_1_out), .out_5(instruction_reg_1_out_5), .out_6(instruction_reg_1_out_6),
    .out_7(instruction_reg_1_out_7), .Flag_register(alu_and_regesters_1_out_8), .out_4(out_1));
  _8bit_counter u_8bit_counter_1 (
    .in_2(out_5), .out_5(out_6), .in_4(clock_1_out), .in_3(instruction_reg_1_out_7[2]),
    .in_1(instruction_reg_1_out_7[3]));
  Multiplexer #(.select(2), .width(8), .enable("false")) multiplexer_1 (
    .in0(8'h7), .in1(alu_and_regesters_1_out_6), .in2(out_4), .in3(out_6), .out(multiplexer_1_out),
    .sel(instruction_reg_1_out_7[1:0]));
  alu_and_regesters alu_and_regesters_1 (
    .in_1(instruction_reg_1_out_5), .in_2(instruction_reg_1_out_6), .in_4(clock_1_out), .out_7(out_2),
    .out_9(out_3), .out_10(out_4), .in_3(out_5), .out_6(alu_and_regesters_1_out_6),
    .out_8(alu_and_regesters_1_out_8), .in_5(instruction_reg_1_out_7[6]), .out_11(out_5));
  not not_1 (not_1_out, clock_1_out);
  RAM #(.bus("separate")) ram_1 (
    .addr(multiplexer_1_out), .din(out_5), .data(out_5), .str(instruction_reg_1_out_7[5]), .sel(1'b1),
    .clk(not_1_out), .ld(instruction_reg_1_out_7[4]));  // open: clr
  // Probe on out_2
endmodule

module _8bit_reg (
  input  [7:0] in_1,
  input  [7:0] in_2,
  input  clk,
  input  select,
  input  out_enable,
  input  _0___data_bus,
  output [7:0] out_7,
  output [7:0] out_8
);

  wire and_1_out;
  wire [7:0] multiplexer_1_out;

  and and_1 (and_1_out, clk, select);
  Multiplexer #(.width(8), .enable("false")) multiplexer_1 (
    .in0(in_1), .in1(in_2), .out(multiplexer_1_out), .sel(_0___data_bus));
  D_Flip_Flop #(.trigger("falling")) d_ff_1 (
    .clk(and_1_out), .D(multiplexer_1_out[0]), .Q(out_7[0]));  // open: Qn, preset, en, reset
  D_Flip_Flop #(.trigger("falling")) d_ff_2 (
    .clk(and_1_out), .D(multiplexer_1_out[1]), .Q(out_7[1]));  // open: Qn, preset, en, reset
  D_Flip_Flop #(.trigger("falling")) d_ff_3 (
    .clk(and_1_out), .D(multiplexer_1_out[2]), .Q(out_7[2]));  // open: Qn, preset, en, reset
  D_Flip_Flop #(.trigger("falling")) d_ff_4 (
    .clk(and_1_out), .D(multiplexer_1_out[3]), .Q(out_7[3]));  // open: Qn, preset, en, reset
  D_Flip_Flop #(.trigger("falling")) d_ff_5 (
    .clk(and_1_out), .D(multiplexer_1_out[4]), .Q(out_7[4]));  // open: Qn, preset, en, reset
  D_Flip_Flop #(.trigger("falling")) d_ff_6 (
    .clk(and_1_out), .D(multiplexer_1_out[5]), .Q(out_7[5]));  // open: Qn, preset, en, reset
  D_Flip_Flop #(.trigger("falling")) d_ff_7 (
    .clk(and_1_out), .D(multiplexer_1_out[6]), .Q(out_7[6]));  // open: Qn, preset, en, reset
  D_Flip_Flop #(.trigger("falling")) d_ff_8 (
    .clk(and_1_out), .D(multiplexer_1_out[7]), .Q(out_7[7]));  // open: Qn, preset, en, reset
  assign out_8 = out_enable ? out_7 : 8'bz;  // Controlled_Buffer controlled_buffer_1

  // Notes on the sheet:
  //   data bus
  //   alu
  //   1 -> ALU
endmodule

module ALU (
  input  [7:0] in_1,
  input  [6:0] in_2,
  input  [7:0] in_3,
  input  in_4,
  output [7:0] out_5,
  output [7:0] out_6,
  output [1:0] out_7
);

  wire adder_1_cout, and_1_out, nor_1_out, not_1_out, not_2_out, not_3_out, not_4_out, not_5_out, not_6_out,
       not_7_out, not_8_out, not_9_out, not_10_out, not_11_out, not_12_out;
  wire [7:0] adder_1_out, and_2_out, controled_inv_1_out_3, controled_inv_2_out_3, multiplexer_1_out,
       multiplexer_2_out, multiplexer_3_out;

  not not_1 (not_1_out, in_4);
  not not_2 (not_2_out, not_1_out);
  not not_3 (not_3_out, not_2_out);
  not not_4 (not_4_out, not_3_out);
  not not_5 (not_5_out, not_6_out);
  not not_6 (not_6_out, not_4_out);
  Pull_Resistor pull_resistor_1 (.node(in_3));
  not not_7 (not_7_out, not_9_out);
  not not_8 (not_8_out, not_7_out);
  not not_9 (not_9_out, not_5_out);
  Multiplexer #(.width(8), .enable("false")) multiplexer_1 (
    .in0(in_1), .in1({8{1'b0}}), .out(multiplexer_1_out), .sel(in_2[0]));
  controled_inv controled_inv_1 (.in_1(multiplexer_1_out), .in_2(in_2[1]), .out_3(controled_inv_1_out_3));
  controled_inv controled_inv_2 (.in_1(multiplexer_2_out), .in_2(in_2[3]), .out_3(controled_inv_2_out_3));
  Multiplexer #(.width(8), .enable("false")) multiplexer_2 (
    .in0(in_3), .in1({8{1'b0}}), .out(multiplexer_2_out), .sel(in_2[2]));
  not not_10 (not_10_out, not_8_out);
  not not_11 (not_11_out, not_10_out);
  and and_1 (and_1_out, in_4, not_12_out);
  not not_12 (not_12_out, not_11_out);
  Adder adder_1 (
    .a(controled_inv_1_out_3), .b(controled_inv_2_out_3), .out(adder_1_out), .cout(adder_1_cout));  // open: cin
  assign and_2_out = controled_inv_1_out_3 & controled_inv_2_out_3;  // AND_Gate and_2, 8 bits wide
  Multiplexer #(.width(8), .enable("false")) multiplexer_3 (
    .in0(adder_1_out), .in1(and_2_out), .out(multiplexer_3_out), .sel(in_2[5]));
  controled_inv controled_inv_3 (.in_1(multiplexer_3_out), .in_2(in_2[4]), .out_3(out_5));
  assign out_6 = in_2[6] ? out_5 : 8'bz;  // Controlled_Buffer controlled_buffer_1
  nor nor_1 (nor_1_out, out_5[0], out_5[1], out_5[2], out_5[3], out_5[4], out_5[5], out_5[6], out_5[7]);
  D_Flip_Flop #(.trigger("falling")) d_ff_1 (
    .clk(and_1_out), .D(nor_1_out), .Q(out_7[0]));  // open: Qn, preset, en, reset
  D_Flip_Flop #(.trigger("falling")) d_ff_2 (
    .clk(and_1_out), .D(adder_1_cout), .Q(out_7[1]));  // open: Qn, preset, en, reset

  // Notes on the sheet:
  //   X
  //   Z x
  //   INV X
  //   Y
  //   Z y
  //   INV Y
  //   INV out
  //   X+Y||X&Y
  //   0           1
endmodule

module controled_inv (
  input  [7:0] in_1,
  input  in_2,
  output [7:0] out_3
);

  xor xor_1 (out_3[0], in_1[0], in_2);
  xor xor_2 (out_3[1], in_1[1], in_2);
  xor xor_3 (out_3[2], in_1[2], in_2);
  xor xor_4 (out_3[3], in_1[3], in_2);
  xor xor_5 (out_3[4], in_1[4], in_2);
  xor xor_6 (out_3[5], in_1[5], in_2);
  xor xor_7 (out_3[6], in_1[6], in_2);
  xor xor_8 (out_3[7], in_1[7], in_2);
endmodule

module _8bit_counter (
  input  in_1,
  input  [7:0] in_2,
  input  in_3,
  input  in_4,
  output [7:0] out_5
);

  wire and_1_out, and_2_out;

  and and_1 (and_1_out, in_1, in_3);
  and and_2 (and_2_out, ~in_1, in_3);  // AND_Gate
  Counter #(.ongoal("continue"), .trigger("falling")) counter_1 (
    .load(and_1_out), .D(in_2), .count(and_2_out), .Q(out_5), .clk(in_4));  // open: carry, clr
endmodule

module _3bit_counter (
  input  in_1,
  input  in_2,
  output out_3,
  output out_4,
  output out_5
);

  wire d_ff_1_q, d_ff_2_qn, d_ff_3_qn, d_ff_4_qn, not_1_out;

  D_Flip_Flop #(.trigger("falling")) d_ff_1 (
    .clk(in_1), .D(in_2), .Q(d_ff_1_q), .reset(not_1_out));  // open: Qn, preset, en
  not not_1 (not_1_out, in_2);
  D_Flip_Flop #(.trigger("falling")) d_ff_2 (
    .clk(in_1), .D(d_ff_2_qn), .Q(out_3), .Qn(d_ff_2_qn), .reset(d_ff_1_q));  // open: preset, en
  D_Flip_Flop #(.trigger("falling")) d_ff_3 (
    .clk(out_3), .D(d_ff_3_qn), .Q(out_4), .Qn(d_ff_3_qn), .reset(d_ff_1_q));  // open: preset, en
  D_Flip_Flop #(.trigger("falling")) d_ff_4 (
    .clk(out_4), .D(d_ff_4_qn), .Q(out_5), .Qn(d_ff_4_qn), .reset(d_ff_1_q));  // open: preset, en
endmodule

module instruction_reg (
  input  [7:0] clk,
  input  in_2,
  input  [1:0] Flag_register,
  output [12:0] out_4,
  output [6:0] out_5,
  output [6:0] out_6,
  output [8:0] out_7
);

  wire and_1_out, nor_1_out, not_1_out, not_2_out, not_3_out, not_4_out, not_5_out, not_6_out, not_7_out,
       not_8_out, not_9_out, not_10_out, not_11_out, not_12_out;
  wire [23:23] rom_1_data;

  _3bit_counter u_3bit_counter_1 (
    .in_1(in_2), .out_3(out_4[10]), .out_4(out_4[11]), .in_2(rom_1_data[23]), .out_5(out_4[12]));
  nor nor_1 (nor_1_out, out_4[10], out_4[11], out_4[12]);
  not not_1 (not_1_out, not_2_out);
  not not_2 (not_2_out, not_3_out);
  not not_3 (not_3_out, nor_1_out);
  not not_4 (not_4_out, not_5_out);
  not not_5 (not_5_out, not_1_out);
  _8bit_reg u_8bit_reg_1 (
    .clk(and_1_out), .select(and_1_out), .out_7(out_4[9:2]), .in_1(clk), ._0___data_bus(1'b0));  // open: out_8, out_enable, in_2
  not not_6 (not_6_out, not_4_out);
  not not_7 (not_7_out, not_8_out);
  not not_8 (not_8_out, not_6_out);
  not not_9 (not_9_out, not_10_out);
  not not_10 (not_10_out, not_7_out);
  not not_11 (not_11_out, not_9_out);
  and and_1 (and_1_out, nor_1_out, not_12_out);
  not not_12 (not_12_out, not_11_out);
  ROM #(.addrWidth(13), .dataWidth(24)) rom_1 (
    .addr({out_4[12:2], Flag_register}), .data({rom_1_data[23], out_7, out_6, out_5}), .sel(1'b1));

  assign out_4[1:0] = Flag_register;

  // Notes on the sheet:
  //   data bus
  //   contents of rom_1 (hex, n*v repeats v):
  //   1024*5c000 4*85c080 4*85c400 4*85d000 4*90ca80 4*90ca92 4*90e280 4*90e292 4*80c000 4*87c000 80c000
  //   87c000 80c000 87c000 80c000 80c000 87c000 87c000 4*4c080 4*4d000 4*90c29e 4*90c28c 1008*7 4*854084
  //   4*898100 6092*7
  //   ALU controll
  //   Register controll
  //   Ram IP SP controll
endmodule

module alu_and_regesters (
  input  [6:0] in_1,
  input  [6:0] in_2,
  input  [7:0] in_3,
  input  in_4,
  input  in_5,
  output [7:0] out_6,
  output [7:0] out_7,
  output [1:0] out_8,
  output [7:0] out_9,
  output [7:0] out_10,
  output [7:0] out_11
);

  wire and_2_out, and_3_out, or_1_out, or_2_out;
  wire [7:0] n8bit_reg_1_out_8;

  or or_1 (or_1_out, in_2[1], in_2[4], in_2[6]);
  or or_2 (or_2_out, in_2[0], in_2[3], in_2[5]);
  // AND_Gate and_1 is placed but not wired
  _8bit_reg u_8bit_reg_1 (
    .clk(in_4), .select(in_2[0]), .out_8(n8bit_reg_1_out_8), .out_enable(in_2[1]), .out_7(out_7),
    .in_1(n8bit_reg_1_out_8), .in_2(out_6), ._0___data_bus(in_2[2]));
  _8bit_reg u_8bit_reg_2 (
    .clk(in_4), .select(in_2[3]), .out_8(n8bit_reg_1_out_8), .out_enable(in_2[4]), .out_7(out_9),
    .in_1(n8bit_reg_1_out_8), ._0___data_bus(1'b0));  // open: in_2
  _8bit_reg u_8bit_reg_3 (
    .clk(in_4), .select(in_2[5]), .out_8(n8bit_reg_1_out_8), .out_enable(in_2[6]), .out_7(out_10),
    .in_1(n8bit_reg_1_out_8), ._0___data_bus(1'b0));  // open: in_2
  and and_2 (and_2_out, or_1_out, ~or_2_out);  // AND_Gate
  and and_3 (and_3_out, ~or_1_out, or_2_out);  // AND_Gate
  ALU alu_1 (
    .in_1(out_7), .in_3(n8bit_reg_1_out_8), .out_6(n8bit_reg_1_out_8), .in_2(in_1), .out_5(out_6),
    .in_4(in_5), .out_7(out_8));
  assign n8bit_reg_1_out_8 = and_3_out ? in_3 : 8'bz;  // Controlled_Buffer controlled_buffer_1
  assign out_11 = and_2_out ? n8bit_reg_1_out_8 : 8'bz;  // Controlled_Buffer controlled_buffer_2

  // Notes on the sheet:
  //   out
  //   in
endmodule

module _8bit27seg (
  input  [7:0] in_1,
  output [3:0] out_2,
  output [3:0] out_3
);

  Hex_Digit_Display hex_digit_display_1 (.value(in_1[7:4]));  // open: dp
  Hex_Digit_Display hex_digit_display_2 (.value(in_1[3:0]));  // open: dp

  assign out_2 = in_1[3:0];
  assign out_3 = in_1[7:4];
endmodule
